# Fritzing sketch google-plant (saved by Fritzing 0.9.5d)
breadboards: 1

parts:
  R1 = Photocell (LDR) [package=THT]
  J1 = male pin header, 3 pins [form="♂ (male)"]
  R2 = Resistor [tolerance=±5% resistance=10k package=THT]
  Capacitive_Soil_Moisture_Sensor1 = DFRobot Capacitive Soil Moisture Sensor V1.0 [part_number=SEN0193]
  Part1 = KY-016 RGB Full Color LED Module [package="Breakout board"]
  M1 = DOIT Esp32 DevKit v1 (30 pins long, 11 pins width) [part_number=ESP32S-PIN30]

nets:
  N1: R1.pin_0, J1.pin2, Capacitive_Soil_Moisture_Sensor1.VCC, M1.D13
  N2: R1.pin_1, R2.Pin_1, M1.VP
  N3: J1.pin1, Capacitive_Soil_Moisture_Sensor1.A, M1.VN
  GND: J1.pin3, R2.Pin_0, Capacitive_Soil_Moisture_Sensor1.GND, Part1.-, M1.GND, M1.D33
  N4: Part1.R, M1.D12
  N5: Part1.G, M1.D14
  N6: Part1.B, M1.D27

notes:
  RGB Pins might be swapped
  R: G12
  G: G14
  B: G27
  Config Interrupt Pin: G33 -> GND

custom parts:
  DFRobot Capacitive Soil Moisture Sensor V1.0: DFRobot Capacitive Soil Moisture Sensor V1.0 This product measures soil moisture levels by capacitive sensing, rather than resistive sensing like other types of moisture sensor. It is made of a corrosion resistant material giving it a long service life. Insert it into soil and impress your friends with the real-time soil moisture data! The product includes an on-board voltage regulator which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
  KY-016 RGB Full Color LED Module: KY-016 Arduino full color 5mm RGB LED, different colors can be obtained by mixing the three primary colors.
  DOIT Esp32 DevKit v1 (30 pins long, 11 pins width): The DOIT Esp32 DevKit v1 is one of the development board created by DOIT to evaluate the ESP-WROOM-32 module. It is based on the ESP32 microcontroller that boasts Wifi, Bluetooth, Ethernet and Low Power support all in a single chip. (vanepp) made breadboard work, adjusted pin numbering and labels and reduced size of schematic and cleaned up pcb. This chip is 30pins long (2 x15) and 11 pins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
